// Digital circuit SOP.dig as structural Verilog
module SOP (
  input  A,
  input  B,
  input  C,
  input  D,
  output Y
);

  wire and_1_out, and_2_out, not_1_out, not_2_out, not_3_out, not_4_out, or_1_out, or_3_out;

  not not_1 (not_1_out, A);
  not not_2 (not_2_out, B);
  not not_3 (not_3_out, C);
  not not_4 (not_4_out, D);
  and and_1 (and_1_out, D, not_1_out, D, D);
  and and_2 (and_2_out, not_4_out, A, not_4_out, not_4_out);
  or or_1 (or_1_out, and_1_out, and_1_out, and_2_out, and_2_out);
  or or_2 (Y, or_3_out, or_1_out);
  or or_3 (or_3_out, and_1_out, and_1_out, and_2_out);

  // Notes on the sheet:
  //   A: MSB
  //   D: LSB
  //   Use A as the most-significant bit and 
  //   D as the least-significant bit.
endmodule

/* Test case:
A B C D Y
0 0 0 0 X
0 0 0 1 1
*/
